// Logisim project projeto.circ as structural Verilog: 13 circuits, main circuit projeto_main
module projeto_main (
  input  A,
  input  B,
  input  [3:0] in_3,
  output S
);

  wire meio_subtrator_1_s, xor_1_s;

  \xor  xor_1 (.A(A), .B(B), .S(xor_1_s));
  meio_subtrator meio_subtrator_1 (.A(A), .B(B), .S(meio_subtrator_1_s));  // open: Tout
  Multiplexer #(.select(4)) multiplexer_1 (
    .in1(xor_1_s), .in2(meio_subtrator_1_s), .in12(1'b0), .in13(1'b0), .in14(1'b0), .in15(1'b0), .out(S),
    .sel(in_3));  // open: in0, in3, in4, in5, in6, in7, in8, in9, in10, in11, en
endmodule

module meio_somador (
  input  A,
  input  B,
  output Soma,
  output CarryOut
);

  xor xor_1 (Soma, A, B);
  and and_1 (CarryOut, A, B);
endmodule

module meio_subtrator (
  input  A,
  input  B,
  output S,
  output Tout
);

  xor xor_1 (S, A, B);
  and and_1 (Tout, B, ~A);  // AND_Gate
endmodule

module multiplicacao (
  input  A1,
  input  A0,
  input  B1,
  input  B0,
  output P3,
  output P2,
  output P1,
  output P0
);

  wire and_1_out, and_2_out, and_3_out, meio_somador_2_carryout;

  and and_1 (and_1_out, A1, B1);
  meio_somador meio_somador_1 (.A(meio_somador_2_carryout), .B(and_1_out), .Soma(P2), .CarryOut(P3));
  and and_2 (and_2_out, A1, B0);
  meio_somador meio_somador_2 (.A(and_3_out), .B(and_2_out), .Soma(P1), .CarryOut(meio_somador_2_carryout));
  and and_3 (and_3_out, A0, B1);
  and and_4 (P0, A0, B0);
endmodule

module \and  (
  input  A,
  input  B,
  output S
);

  and and_1 (S, A, B);
endmodule

module \or  (
  input  A,
  input  B,
  output S
);

  or or_1 (S, A, B);
endmodule

module inversora (
  input  B,
  output S
);

  not not_1 (S, B);
endmodule

module \xor  (
  input  A,
  input  B,
  output S
);

  wire and_1_out, and_2_out, not_1_out, not_2_out;

  not not_1 (not_1_out, B);
  not not_2 (not_2_out, A);
  and and_1 (and_1_out, A, not_1_out);
  and and_2 (and_2_out, not_2_out, B);
  or or_1 (S, and_1_out, and_2_out);
endmodule

module deslocamento_esquerda (
  input  A,
  input  D,
  output S
);

  Shifter #(.width(1)) shifter_1 (.in(A), .\dist (D), .out(S));
endmodule

module deslocamento_direita (
  input  A,
  input  D,
  output S
);

  Shifter #(.width(1)) shifter_1 (.in(A), .\dist (D), .out(S));
endmodule

module \nor  (
  input  A,
  input  B,
  output S
);

  wire or_1_out;

  not not_1 (S, or_1_out);
  or or_1 (or_1_out, A, B);
endmodule

module \nand  (
  input  A,
  input  B,
  output S
);

  wire and_1_out;

  and and_1 (and_1_out, A, B);
  not not_1 (S, and_1_out);
endmodule

module \xnor  (
  input  A,
  input  B,
  output S
);

  wire xor_1_s;

  \xor  xor_1 (.A(A), .B(B), .S(xor_1_s));
  not not_1 (S, xor_1_s);
endmodule
