// Logisim project Relatorio 01.circ as structural Verilog: 6 circuits, main circuit subtrator
module subtrator (
  input  A,
  input  B,
  output S,
  output Tout
);

  xor xor_1 (S, A, B);
  and and_1 (Tout, B, ~A);  // AND_Gate
endmodule

module somador (
  input  A,
  input  B,
  output Soma,
  output CarryOut
);

  xor xor_1 (Soma, A, B);
  and and_1 (CarryOut, A, B);
endmodule

module ex01 (
  input  in_1,
  input  in_2,
  input  in_3,
  input  in_4,
  output Output,
  output COut,
  output TOut
);

  wire somador_1_soma, subtrator_1_s;

  subtrator subtrator_1 (.A(in_1), .B(in_2), .S(subtrator_1_s), .Tout(TOut));
  somador somador_1 (.A(in_1), .B(in_2), .Soma(somador_1_soma), .CarryOut(COut));
  Multiplexer multiplexer_1 (.in0(subtrator_1_s), .in1(somador_1_soma), .out(Output), .sel(in_3), .en(in_4));
endmodule

module subtrator_completo (
  input  A,
  input  B,
  input  BorrowIN,
  output Sub,
  output BorrowOut
);

  wire subtrator_1_s, subtrator_1_tout, subtrator_2_tout;

  subtrator subtrator_1 (.A(A), .B(B), .S(subtrator_1_s), .Tout(subtrator_1_tout));
  subtrator subtrator_2 (.A(subtrator_1_s), .B(BorrowIN), .S(Sub), .Tout(subtrator_2_tout));
  or or_1 (BorrowOut, subtrator_2_tout, subtrator_1_tout);
endmodule

module somador_completo (
  input  A,
  input  B,
  input  CarryIN,
  output Soma,
  output CarryOut
);

  wire somador_1_carryout, somador_1_soma, somador_2_carryout;

  somador somador_1 (.A(A), .B(B), .Soma(somador_1_soma), .CarryOut(somador_1_carryout));
  somador somador_2 (.A(somador_1_soma), .B(CarryIN), .Soma(Soma), .CarryOut(somador_2_carryout));
  or or_1 (CarryOut, somador_2_carryout, somador_1_carryout);
endmodule

module ex02 (
  input  A,
  input  B,
  input  C_B_in,
  input  in_4,
  input  in_5,
  output out_6,
  output BOut,
  output COut
);

  wire somador_completo_1_soma, subtrator_completo_1_sub;

  subtrator_completo subtrator_completo_1 (
    .A(A), .B(B), .BorrowIN(C_B_in), .Sub(subtrator_completo_1_sub), .BorrowOut(BOut));
  somador_completo somador_completo_1 (.A(A), .B(B), .CarryIN(C_B_in), .Soma(somador_completo_1_soma), .CarryOut(COut));
  Multiplexer multiplexer_1 (
    .in0(subtrator_completo_1_sub), .in1(somador_completo_1_soma), .out(out_6), .sel(in_4), .en(in_5));
endmodule
