// Logisim project Somador.circ as structural Verilog: 2 circuits, main circuit somador
module somador (
  input  A,
  input  B,
  output Soma,
  output CarryOut
);

  xor xor_1 (Soma, A, B);
  and and_1 (CarryOut, A, B);
endmodule

module somador_completo (
  input  A,
  input  B,
  input  CarryIN,
  output Soma,
  output CarryOut
);

  wire somador_1_carryout, somador_1_soma, somador_2_carryout;

  somador somador_1 (.A(A), .B(B), .Soma(somador_1_soma), .CarryOut(somador_1_carryout));
  somador somador_2 (.A(somador_1_soma), .B(CarryIN), .Soma(Soma), .CarryOut(somador_2_carryout));
  or or_1 (CarryOut, somador_2_carryout, somador_1_carryout);
endmodule
