// Logisim project Subtrator.circ as structural Verilog
module subtrator (
  input  A,
  input  B,
  output S,
  output Tout
);

  xor xor_1 (S, A, B);
  and and_1 (Tout, B, ~A);  // AND_Gate
endmodule

module subtrator_completo (
  input  A,
  input  B,
  input  BorrowIN,
  output Sub,
  output BorrowOut
);

  wire subtrator_1_s, subtrator_1_tout, subtrator_2_tout;

  subtrator subtrator_1 (.A(A), .B(B), .S(subtrator_1_s), .Tout(subtrator_1_tout));
  subtrator subtrator_2 (.A(subtrator_1_s), .B(BorrowIN), .S(Sub), .Tout(subtrator_2_tout));
  or or_1 (BorrowOut, subtrator_2_tout, subtrator_1_tout);
endmodule
