// Logisim project Relatorio 02.circ as structural Verilog: 3 circuits, main circuit meio_somador
module meio_somador (
  input  A,
  input  B,
  output Soma,
  output CarryOut
);

  xor xor_1 (Soma, A, B);
  and and_1 (CarryOut, A, B);
endmodule

module ex02 (
  input  A1,
  input  A0,
  input  B1,
  input  B0,
  output P3,
  output P2,
  output P1,
  output P0
);

  wire and_1_out, and_2_out, and_3_out, meio_somador_2_carryout;

  and and_1 (and_1_out, A1, B1);
  meio_somador meio_somador_1 (.A(meio_somador_2_carryout), .B(and_1_out), .Soma(P2), .CarryOut(P3));
  and and_2 (and_2_out, A1, B0);
  meio_somador meio_somador_2 (.A(and_3_out), .B(and_2_out), .Soma(P1), .CarryOut(meio_somador_2_carryout));
  and and_3 (and_3_out, A0, B1);
  and and_4 (P0, A0, B0);
endmodule

module ex03 (
  input  [3:0] D,
  input  Carga,
  input  Clear,
  output [3:0] Q
);

  wire Clock_out, multiplexer_1_out, multiplexer_2_out, multiplexer_3_out, multiplexer_4_out;

  Clock Clock (.out(Clock_out));
  Multiplexer multiplexer_1 (.in0(Q[0]), .in1(D[0]), .out(multiplexer_1_out), .sel(Carga));  // open: en
  D_Flip_Flop d_ff_1 (.clk(Clock_out), .D(multiplexer_1_out), .Q(Q[0]), .reset(Clear));  // open: Qn, preset, en
  Multiplexer multiplexer_2 (.in0(Q[1]), .in1(D[1]), .out(multiplexer_2_out), .sel(Carga));  // open: en
  D_Flip_Flop d_ff_2 (.clk(Clock_out), .D(multiplexer_2_out), .Q(Q[1]), .reset(Clear));  // open: Qn, preset, en
  Multiplexer multiplexer_3 (.in0(Q[2]), .in1(D[2]), .out(multiplexer_3_out), .sel(Carga));  // open: en
  D_Flip_Flop d_ff_3 (.clk(Clock_out), .D(multiplexer_3_out), .Q(Q[2]), .reset(Clear));  // open: Qn, preset, en
  Multiplexer multiplexer_4 (.in0(Q[3]), .in1(D[3]), .out(multiplexer_4_out), .sel(Carga));  // open: en
  D_Flip_Flop d_ff_4 (.clk(Clock_out), .D(multiplexer_4_out), .Q(Q[3]), .reset(Clear));  // open: Qn, preset, en
endmodule
