// Logisim project Aula 1810.circ as structural Verilog: 1 circuit, main circuit main
module main (
  input  [3:0] in_1,
  input  \Habilita_gravação ,
  output [5:0] funct,
  output [4:0] SA,
  output [31:0] Dado_a_ser_gravado,
  output [5:0] out_6,
  output [4:0] Origem_2,
  output [4:0] Origem_1,
  output [4:0] Reg_destino
);

  wire clock_1_out, clock_2_out, registerfile_1_p7, registerfile_1_p8;
  wire [31:0] adder_1_out, register_1_q;

  Adder #(.width(32)) adder_1 (.a(register_1_q), .b(32'h4), .out(adder_1_out));  // open: cin, cout
  Register #(.width(32)) register_1 (.D(adder_1_out), .Q(register_1_q), .clk(clock_1_out));  // open: en, clr
  Clock clock_1 (.out(clock_1_out));
  // MIPSProgramROM mipsprogramrom_1: pin names not known; wires that end beside it: register_1_q, {out_6, Origem_1, Origem_2, Reg_destino, SA, funct}
  Clock clock_2 (.out(clock_2_out));
  // RegisterFile registerfile_1: pin names not known; wires that end beside it: Dado_a_ser_gravado, clock_2_out, \Habilita_gravação , Reg_destino, Origem_1, Origem_2, registerfile_1_p7, registerfile_1_p8
  // Mips_ALU mips_alu_1: pin names not known; wires that end beside it: registerfile_1_p7, registerfile_1_p8, in_1, Dado_a_ser_gravado

  // Notes on the sheet:
  //   Memoria de programa
  //   0x21
  //   0x00
  //   $6
  //   Destino
  //   Origem 2
  //   $2
  //   Origem 1
  //   $13
  //   Opcode
  //   0x00
endmodule
